# Fritzing sketch board (saved by Fritzing 0.9.3b)
perfboards: 1

parts:
  U2 = NodeMCU V1.0
  LM7805_IC1 = Voltage Regulator [package=to-220-alt]
  J1 = Power Jack [package=power_jack_pth_lock]  # not connected
  IC1 = ULN2003A [package="DIP16 [THT]"]
  Mod1 = KY-018 Photoresistor Module [package="Breakout board"]

nets:
  N1: U2.3V3, Mod1.-
  GND: U2.GND, LM7805_IC1.IN, IC1.Out_1, Mod1.Vin
  N2: U2.D6, IC1.Out_6
  N3: U2.D7, IC1.Out_7
  N4: U2.D8, IC1.COM_-_Common
  N5: U2.Vin, LM7805_IC1.OUT
  N6: U2.A0, Mod1.S
  N7: LM7805_IC1.GND, IC1.In_1

custom parts:
  NodeMCU V1.0: ESP8266 based NodeMCU
  KY-018 Photoresistor Module: KY-018 Photoresistor module, used to measure light intensity. It can determine the presence or absence of light.
